// Logisim project trab_v1.circ as structural Verilog: 7 circuits, main circuit PC
module main (
);

  wire ALU_SRC, and_1_out, BRANCH, CLK, JR, JUMP, MEM_WE, W_R0, WE, zero_detector_1_out_2;
  wire [1:0] multiplexer_3_out, W_SRC;
  wire [1:1] or_1_out;
  wire [2:0] ALU_OP;
  wire [7:0] adder_1_out, adder_2_out, banco_de_registradores_1_a, banco_de_registradores_1_b,
       dual_port_ram_1_data, dual_port_ram_1_instr, multiplexer_1_out, multiplexer_2_out, multiplexer_4_out,
       pc_1_pc_atual, sign_extend_1_s, ula_1_s;

  Adder adder_1 (.a(8'h1), .b(pc_1_pc_atual), .out(adder_1_out), .cin(1'b0));  // open: cout
  Adder adder_2 (.a(sign_extend_1_s), .b(pc_1_pc_atual), .out(adder_2_out), .cin(1'b0));  // open: cout
  or or_1 (or_1_out[1], JR, and_1_out);
  Multiplexer #(.select(2), .width(8)) multiplexer_1 (
    .in0(adder_1_out), .in1(adder_2_out), .in2(banco_de_registradores_1_b), .out(multiplexer_1_out),
    .sel({or_1_out[1], JUMP}));  // open: in3
  PC pc_1 (.CLK(CLK), .PC_prox(multiplexer_1_out), .PC_atual(pc_1_pc_atual));
  and and_1 (and_1_out, zero_detector_1_out_2, BRANCH);
  // Probe on pc_1_pc_atual
  Clock clock_1 (.out(CLK));
  dual_port_ram dual_port_ram_1 (
    .addr(banco_de_registradores_1_b), .pc(pc_1_pc_atual), .d(banco_de_registradores_1_a), .w(MEM_WE),
    .instr(dual_port_ram_1_instr), .data(dual_port_ram_1_data));
  // Probe on dual_port_ram_1_instr
  Multiplexer #(.select(2), .width(8)) multiplexer_2 (
    .in0(ula_1_s), .in1(dual_port_ram_1_data), .in2(banco_de_registradores_1_b), .in3(adder_2_out),
    .out(multiplexer_2_out), .sel(W_SRC));
  // Probe on dual_port_ram_1_data
  // Probe on dual_port_ram_1_instr[7:4]
  // Probe on dual_port_ram_1_instr[1:0]
  // Probe on dual_port_ram_1_instr[3:2]
  ROM #(.addrWidth(4), .dataWidth(12)) CONTROL_MEMORY (
    .addr(dual_port_ram_1_instr[7:4]), .data({WE, W_R0, ALU_SRC, ALU_OP, W_SRC, MEM_WE, BRANCH, JUMP, JR}));
  Multiplexer #(.width(2)) multiplexer_3 (
    .in0(dual_port_ram_1_instr[3:2]), .in1(2'b00), .out(multiplexer_3_out), .sel(W_R0));
  // Probe on dual_port_ram_1_instr[3:0]
  Banco_de_registradores banco_de_registradores_1 (
    .WE(WE), .W_END(multiplexer_3_out), .ENTRADA(multiplexer_2_out), .CLK(CLK), .A_END(multiplexer_3_out),
    .B_END(dual_port_ram_1_instr[1:0]), .A(banco_de_registradores_1_a), .B(banco_de_registradores_1_b));
  Sign_extend sign_extend_1 (.Imm(dual_port_ram_1_instr[3:0]), .S(sign_extend_1_s));
  Zero_detector zero_detector_1 (.in_1(banco_de_registradores_1_a), .out_2(zero_detector_1_out_2));
  Multiplexer #(.width(8)) multiplexer_4 (
    .in0(banco_de_registradores_1_b), .in1(sign_extend_1_s), .out(multiplexer_4_out), .sel(ALU_SRC));
  ULA ula_1 (.Funct(ALU_OP), .A(banco_de_registradores_1_a), .B(multiplexer_4_out), .S(ula_1_s));  // open: ZERO
  // Probe on ALU_OP

  // Notes on the sheet:
  //   contents of CONTROL_MEMORY (hex, n*v repeats v):
  //   4 2 810 8 f00 820 1 c30 800 840 880 8c0 900 940 980 9c0
endmodule

module dual_port_ram (
  input  [7:0] addr,
  input  [7:0] pc,
  input  [7:0] d,
  input  w,
  output [7:0] instr,
  output [7:0] data
);

  wire clock_1_out, or_1_out;
  wire [7:0] multiplexer_1_out;

  Clock clock_1 (.out(clock_1_out));
  or or_1 (or_1_out, w, clock_1_out);
  Multiplexer #(.width(8)) multiplexer_1 (.in0(addr), .in1(pc), .out(multiplexer_1_out), .sel(clock_1_out));
  RAM #(.asyncread("true")) ram_1 (
    .addr(multiplexer_1_out), .we(or_1_out), .oe(1'b1), .clk(clock_1_out), .din(d), .dout(data));
  Register #(.trigger("falling")) pcbuf (.D(data), .en(1'b1), .clk(clock_1_out), .Q(instr));  // open: clr
endmodule

module PC (
  input  [7:0] PC_prox,
  input  CLK,
  output [7:0] PC_atual
);

  Register register_1 (.D(PC_prox), .en(1'b1), .clk(CLK), .Q(PC_atual));  // open: clr
endmodule

module Sign_extend (
  input  [3:0] Imm,
  output [7:0] S
);


  assign S = {{5{Imm[3]}}, Imm[2:0]};
endmodule

module Banco_de_registradores (
  input  [1:0] A_END,
  input  WE,
  input  [1:0] W_END,
  input  [1:0] B_END,
  input  CLK,
  input  [7:0] ENTRADA,
  output [7:0] A,
  output [7:0] B
);

  wire demultiplexer_1_out0, demultiplexer_1_out1, demultiplexer_1_out2, demultiplexer_1_out3;
  wire [7:0] register_1_q, register_2_q, register_3_q, register_4_q;

  Demultiplexer #(.select(2)) demultiplexer_1 (
    .out0(demultiplexer_1_out0), .out1(demultiplexer_1_out1), .out2(demultiplexer_1_out2),
    .out3(demultiplexer_1_out3), .in(WE), .sel(W_END));
  Register register_1 (.D(ENTRADA), .en(demultiplexer_1_out0), .clk(CLK), .Q(register_1_q));  // open: clr
  Register register_2 (.D(ENTRADA), .en(demultiplexer_1_out1), .clk(CLK), .Q(register_2_q));  // open: clr
  Register register_3 (.D(ENTRADA), .en(demultiplexer_1_out2), .clk(CLK), .Q(register_3_q));  // open: clr
  Register register_4 (.D(ENTRADA), .en(demultiplexer_1_out3), .clk(CLK), .Q(register_4_q));  // open: clr
  // Probe on register_1_q
  Multiplexer #(.select(2), .width(8)) multiplexer_1 (
    .in0(register_1_q), .in1(register_2_q), .in2(register_3_q), .in3(register_4_q), .out(A), .sel(A_END));
  Multiplexer #(.select(2), .width(8)) multiplexer_2 (
    .in0(register_1_q), .in1(register_2_q), .in2(register_3_q), .in3(register_4_q), .out(B), .sel(B_END));
endmodule

module Zero_detector (
  input  [7:0] in_1,
  output out_2
);

  nor nor_1 (out_2, in_1[0], in_1[1], in_1[2], in_1[3], in_1[4], in_1[5], in_1[6], in_1[7]);
endmodule

module ULA (
  input  [7:0] A,
  input  [7:0] B,
  input  [2:0] Funct,
  output ZERO,
  output [7:0] S
);

  wire and_2_out;
  wire [7:0] adder_1_out, and_1_out, multiplexer_1_out, not_1_out, or_1_out, shifter_1_out, shifter_2_out,
       xor_1_out;

  assign not_1_out = ~B;  // NOT_Gate not_1, 8 bits wide
  Multiplexer #(.width(8)) multiplexer_1 (.in0(B), .in1(not_1_out), .out(multiplexer_1_out), .sel(and_2_out));
  assign and_1_out = A & B;  // AND_Gate and_1, 8 bits wide
  assign or_1_out = A | B;  // OR_Gate or_1, 8 bits wide
  assign xor_1_out = A ^ B;  // XOR_Gate xor_1, 8 bits wide
  Adder adder_1 (.a(A), .b(multiplexer_1_out), .out(adder_1_out), .cin(and_2_out));  // open: cout
  Shifter shifter_1 (.in(A), .\dist (B[2:0]), .out(shifter_1_out));
  Shifter #(.shift("lr")) shifter_2 (.in(A), .\dist (B[2:0]), .out(shifter_2_out));
  and and_2 (and_2_out, Funct[0], Funct[2]);
  Zero_detector zero_detector_1 (.in_1(S), .out_2(ZERO));
  Multiplexer #(.select(3), .width(8)) multiplexer_2 (
    .in0(not_1_out), .in1(and_1_out), .in2(or_1_out), .in3(xor_1_out), .in4(adder_1_out), .in5(adder_1_out),
    .in6(shifter_1_out), .in7(shifter_2_out), .out(S), .sel(Funct));

  // Notes on the sheet:
  //   000 Not
  //   001 AND
  //   010 OR
  //   011 XOR
  //   100 ADD
  //   101 SUB
  //   110 SL
  //   111 SR
endmodule
