// Logisim project trab_v1.circ as structural Verilog
module PC (
  input  [31:0] PC_prox,
  input  CLK,
  output [31:0] PC_atual
);

  Register #(.width(32)) register_1 (.D(PC_prox), .en(1'b1), .clk(CLK), .Q(PC_atual));  // open: clr
endmodule

module Extensor_sinal_16_bits (
  input  [15:0] Imm,
  output [31:0] S
);


  assign S = {{17{Imm[15]}}, Imm[14:0]};
endmodule

module Banco_de_registradores (
  input  [1:0] A_END,
  input  WE,
  input  [1:0] W_END,
  input  [1:0] B_END,
  input  CLK,
  input  [31:0] ENTRADA,
  output [31:0] A,
  output [31:0] B
);

  wire demultiplexer_1_out0, demultiplexer_1_out1, demultiplexer_1_out2, demultiplexer_1_out3;
  wire [31:0] register_1_q, register_2_q, register_3_q, register_4_q;

  Demultiplexer #(.select(2)) demultiplexer_1 (
    .out0(demultiplexer_1_out0), .out1(demultiplexer_1_out1), .out2(demultiplexer_1_out2),
    .out3(demultiplexer_1_out3), .in(WE), .sel(W_END));
  Register #(.width(32)) register_1 (.D(ENTRADA), .en(demultiplexer_1_out0), .clk(CLK), .Q(register_1_q));  // open: clr
  Register #(.width(32)) register_2 (.D(ENTRADA), .en(demultiplexer_1_out1), .clk(CLK), .Q(register_2_q));  // open: clr
  Register #(.width(32)) register_3 (.D(ENTRADA), .en(demultiplexer_1_out2), .clk(CLK), .Q(register_3_q));  // open: clr
  Register #(.width(32)) register_4 (.D(ENTRADA), .en(demultiplexer_1_out3), .clk(CLK), .Q(register_4_q));  // open: clr
  Multiplexer #(.select(2), .width(32)) multiplexer_1 (
    .in0(register_1_q), .in1(register_2_q), .in2(register_3_q), .in3(register_4_q), .out(A), .sel(A_END));
  Multiplexer #(.select(2), .width(32)) multiplexer_2 (
    .in0(register_1_q), .in1(register_2_q), .in2(register_3_q), .in3(register_4_q), .out(B), .sel(B_END));
endmodule

module Zero_detector_32_bits (
  input  [31:0] in_1,
  output out_2
);

  nor nor_1 (out_2, in_1[0], in_1[1], in_1[2], in_1[3], in_1[4], in_1[5], in_1[6], in_1[7], in_1[8], in_1[9], in_1[10], in_1[11], in_1[12], in_1[13], in_1[14], in_1[15], in_1[16], in_1[17], in_1[18], in_1[19], in_1[20], in_1[21], in_1[22], in_1[23], in_1[24], in_1[25], in_1[26], in_1[27], in_1[28], in_1[29], in_1[30], in_1[31]);
endmodule

module ULA (
  input  [31:0] A,
  input  [31:0] B,
  input  [2:0] Funct,
  output ZERO,
  output [31:0] S
);

  wire and_2_out;
  wire [31:0] adder_1_out, and_1_out, multiplexer_1_out, not_1_out, or_1_out, shifter_1_out, shifter_2_out,
       xor_1_out;

  assign not_1_out = ~B;  // NOT_Gate not_1, 32 bits wide
  Multiplexer #(.width(32)) multiplexer_1 (.in0(B), .in1(not_1_out), .out(multiplexer_1_out), .sel(and_2_out));
  assign and_1_out = A & B;  // AND_Gate and_1, 32 bits wide
  assign or_1_out = A | B;  // OR_Gate or_1, 32 bits wide
  assign xor_1_out = A ^ B;  // XOR_Gate xor_1, 32 bits wide
  Adder #(.width(32)) adder_1 (.a(A), .b(multiplexer_1_out), .out(adder_1_out), .cin(and_2_out));  // open: cout
  Shifter #(.width(32)) shifter_1 (.in(A), .\dist (B[4:0]), .out(shifter_1_out));
  Shifter #(.shift("lr"), .width(32)) shifter_2 (.in(A), .\dist (B[4:0]), .out(shifter_2_out));
  and and_2 (and_2_out, Funct[0], Funct[2]);
  Zero_detector_32_bits zero_detector_32_bits_1 (.in_1(S), .out_2(ZERO));
  Multiplexer #(.select(3), .width(32)) multiplexer_2 (
    .in0(not_1_out), .in1(and_1_out), .in2(or_1_out), .in3(xor_1_out), .in4(adder_1_out), .in5(adder_1_out),
    .in6(shifter_1_out), .in7(shifter_2_out), .out(S), .sel(Funct));
endmodule
